# Fritzing sketch TinyRotayPCB (saved by Fritzing 0.9.3b)
perfboards: 1

parts:
  U1 = attiny85 [package=dip]
  ENCODER1 = Rotary Encoder with Knob
  J1 = rounded female pin header, 4 pins [form="♀ (female rounded)"]
  J2 = rounded female pin header, 4 pins [form="♀ (female rounded)"]
  JP2 = Header 5x2 [package=2x5-ra]
  R1 = Resistor [tolerance=±5% resistance=220 package="2512 [SMD]"]
  R2 = Resistor [tolerance=±5% resistance=220 package="1206 [SMD]"]

nets:
  N1: U1.Pin_1, J1.pin1
  N2: U1.Pin_2, ENCODER1.no_name_yet#3, J1.pin2
  N3: U1.Pin_3, ENCODER1.no_name_yet#1, J1.pin3
  N4: U1.Pin_4, ENCODER1.no_name_yet#2, ENCODER1.no_name_yet#5, J1.pin4, JP2.5, JP2.6, JP2.7, JP2.9
  N5: U1.Pin_5, J2.pin4, R1.Pin_0
  N6: U1.Pin_6, J2.pin3, R2.Pin_0
  N7: U1.Pin_7, ENCODER1.no_name_yet#4, J2.pin2
  N8: U1.Pin_8, J2.pin1, JP2.1, JP2.2, JP2.8
  N9: JP2.3, R1.Pin_1
  N10: JP2.4, R2.Pin_1

custom parts:
  Rotary Encoder with Knob: Rotary Encoder with 1/4" Shaft and Knob
